# Fritzing sketch divider-op-amp (saved by Fritzing 0.9.3b)
circuit board: 8.46667cm x 5.64444cm
breadboards: 1

parts:
  IC1 = 2 MHz rail-to-rail Op Amp [part_number=MCP6273 package="DIP (Dual Inline) [THT]"]
  R2 = Resistor [tolerance=±5% resistance=220 package=THT]
  R1 = Resistor [tolerance=±5% resistance=220 package=THT]

nets:
  N1: IC1.Vin-, IC1.Vout
  N2: IC1.Vin+, R2.Pin_0, R1.Pin_1
  N3: IC1.Vss, IC1.~CS, R2.Pin_1
  N4: IC1.Vdd, R1.Pin_0

custom parts:
  2 MHz rail-to-rail Op Amp: Single-supply rail-to-rail op amp. Datasheet: http://ww1.microchip.com/downloads/en/DeviceDoc/21810f.pdf
