# Fritzing sketch shield (saved by Fritzing 0.9.3b)

parts:
  Part1 = Arduino Prototyping Shield
  IC1 = 2 MHz rail-to-rail Op Amp [part_number=MCP6273 package="DIP (Dual Inline) [THT]"]
  R16 = Resistor [tolerance=±1% resistance=1k package=THT]
  R18 = Resistor [tolerance=±1% resistance=3.3k package=THT]
  R19 = Resistor [tolerance=±1% resistance=10k package=THT]
  R20 = Resistor [tolerance=±1% resistance=33k package=THT]
  R22 = Resistor [tolerance=±1% resistance=330k package=THT]
  R21 = Resistor [tolerance=±1% resistance=100k package=THT]
  R23 = Resistor [tolerance=±1% resistance=1M package=THT]
  R24 = Resistor [tolerance=±1% resistance=10M package=THT]
  J1 = female pin header, 2 pins [form="♀ (female)"]
  J2 = female pin header, 4 pins [form="♀ (female)"]

nets:
  +5V: Part1.+5V, Part1.N$65, IC1.Vdd
  N1: Part1.D8, R21.Pin_0
  N2: Part1.D9, R22.Pin_0
  N3: Part1.D10, R23.Pin_0
  N4: Part1.D11, R24.Pin_0
  N5: Part1.D4, R16.Pin_0
  N6: Part1.D5, R18.Pin_0
  N7: Part1.D6, R19.Pin_0
  N8: Part1.D7, R20.Pin_0
  N9: Part1.A4, Part1.N$61, Part1.N$62, Part1.N$78, Part1.N$79, IC1.Vin-, IC1.Vout
  GND: Part1.GND, Part1.N$55, Part1.N$86, Part1.N$383, IC1.Vss, IC1.~CS, J2.pin3
  N10: Part1.N$43, J2.pin1
  N11: Part1.N$48, IC1.NC#1
  N12: Part1.N$51, J2.pin2
  N13: Part1.N$72, Part1.N$228, Part1.N$242, Part1.N$243, Part1.N$406, Part1.N$409, Part1.N$412, Part1.N$413, Part1.N$414, Part1.N$415, IC1.Vin+, R16.Pin_1, R18.Pin_1, R19.Pin_1, R20.Pin_1, R22.Pin_1, R21.Pin_1, R23.Pin_1, R24.Pin_1, J1.pin1
  N14: Part1.N$84, IC1.NC#5
  N15: Part1.N$380, J2.pin4
  N16: Part1.N$402, J1.pin2

custom parts:
  2 MHz rail-to-rail Op Amp: Single-supply rail-to-rail op amp. Datasheet: http://ww1.microchip.com/downloads/en/DeviceDoc/21810f.pdf
